// Logisim project lab2_part2.circ as structural Verilog: 9 circuits, main circuit main
module main (
  input  SW0,
  input  SW1,
  input  SW2,
  input  SW3
);

  wire hex_decoder_1_s0, hex_decoder_1_s1, hex_decoder_1_s2, hex_decoder_1_s3, hex_decoder_1_s4,
       hex_decoder_1_s5, hex_decoder_1_s6;

  HEX_DECODER hex_decoder_1 (
    .D0(SW0), .D1(SW1), .D2(SW2), .D3(SW3), .s0(hex_decoder_1_s0), .s1(hex_decoder_1_s1),
    .s2(hex_decoder_1_s2), .s3(hex_decoder_1_s3), .s4(hex_decoder_1_s4), .s5(hex_decoder_1_s5),
    .s6(hex_decoder_1_s6));
  _7_Segment_Display u_7_segment_display_1 (
    .g(hex_decoder_1_s6), .f(hex_decoder_1_s5), .a(hex_decoder_1_s0), .b(hex_decoder_1_s1),
    .e(hex_decoder_1_s4), .d(hex_decoder_1_s3), .c(hex_decoder_1_s2));  // open: dp
endmodule

module HEX0 (
  input  D0,
  input  D1,
  input  D2,
  input  D3,
  output S0
);

  wire and_1_out, and_2_out, and_3_out, and_4_out, and_5_out, and_6_out, not_1_out, not_2_out, not_3_out,
       not_4_out;

  not not_1 (not_1_out, D0);
  not not_2 (not_2_out, D1);
  not not_3 (not_3_out, D2);
  not not_4 (not_4_out, D3);
  and and_1 (and_1_out, not_3_out, not_2_out, D3);
  and and_2 (and_2_out, not_4_out, D0, D2);
  and and_3 (and_3_out, not_1_out, not_3_out);
  and and_4 (and_4_out, not_1_out, D1);
  and and_5 (and_5_out, not_4_out, D1);
  and and_6 (and_6_out, D1, D2);
  or or_1 (S0, and_1_out, and_2_out, and_3_out, and_4_out, and_5_out, and_6_out);
endmodule

module HEX1 (
  input  D0,
  input  D1,
  input  D2,
  input  D3,
  output S1
);

  wire and_1_out, and_2_out, and_3_out, and_4_out, and_5_out, and_6_out, not_1_out, not_2_out, not_3_out,
       not_4_out;

  not not_1 (not_1_out, D0);
  not not_2 (not_2_out, D1);
  not not_3 (not_3_out, D2);
  not not_4 (not_4_out, D3);
  and and_1 (and_1_out, D0, D1, not_4_out);
  and and_2 (and_2_out, D0, D3, not_2_out);
  and and_3 (and_3_out, not_2_out, not_1_out, not_4_out);
  and and_4 (and_4_out, not_3_out, not_1_out);
  and and_5 (and_5_out, not_2_out, not_3_out);
  and and_6 (and_6_out, not_4_out, not_3_out);
  or or_1 (S1, and_1_out, and_2_out, and_3_out, and_4_out, and_5_out, and_6_out);
endmodule

module HEX2 (
  input  D0,
  input  D1,
  input  D2,
  input  D3,
  output S2
);

  wire and_1_out, and_2_out, and_3_out, and_4_out, and_5_out, not_1_out, not_2_out, not_3_out;

  not not_1 (not_1_out, D1);
  not not_2 (not_2_out, D2);
  not not_3 (not_3_out, D3);
  and and_1 (and_1_out, not_2_out, D3);
  and and_2 (and_2_out, not_3_out, D2);
  and and_3 (and_3_out, not_2_out, D0);
  and and_4 (and_4_out, D0, not_1_out);
  and and_5 (and_5_out, not_2_out, not_1_out);
  or or_1 (S2, and_2_out, and_4_out, and_5_out, and_3_out, and_1_out);
endmodule

module HEX3 (
  input  D0,
  input  D1,
  input  D2,
  input  D3,
  output S3
);

  wire and_1_out, and_2_out, and_3_out, and_4_out, and_5_out, not_1_out, not_2_out, not_3_out, not_4_out;

  not not_1 (not_1_out, D0);
  not not_2 (not_2_out, D1);
  not not_3 (not_3_out, D2);
  not not_4 (not_4_out, D3);
  and and_1 (and_1_out, D1, D0, not_3_out);
  and and_2 (and_2_out, not_1_out, not_3_out, not_4_out);
  and and_3 (and_3_out, not_1_out, D1, D2);
  and and_4 (and_4_out, not_2_out, D0, D2);
  and and_5 (and_5_out, D3, not_2_out);
  or or_1 (S3, and_2_out, and_3_out, and_4_out, and_1_out, and_5_out);
endmodule

module HEX4 (
  input  D0,
  input  D1,
  input  D2,
  input  D3,
  output S4
);

  wire and_1_out, and_2_out, and_3_out, and_4_out, not_1_out, not_2_out;

  not not_1 (not_1_out, D0);
  not not_2 (not_2_out, D2);
  and and_1 (and_1_out, D0, D1, D3);
  and and_2 (and_2_out, D2, D3);
  and and_3 (and_3_out, D1, not_1_out);
  and and_4 (and_4_out, not_1_out, not_2_out);
  or or_1 (S4, and_1_out, and_2_out, and_3_out, and_4_out);
endmodule

module HEX5 (
  input  D0,
  input  D1,
  input  D2,
  input  D3,
  output S5
);

  wire and_1_out, and_2_out, and_3_out, and_4_out, and_5_out, not_1_out, not_2_out, not_3_out, not_4_out;

  not not_1 (not_1_out, D0);
  not not_2 (not_2_out, D1);
  not not_3 (not_3_out, D2);
  not not_4 (not_4_out, D3);
  and and_1 (and_1_out, not_1_out, D1, D2);
  and and_2 (and_2_out, not_4_out, not_2_out, D2);
  and and_3 (and_3_out, not_2_out, not_1_out, not_4_out);
  and and_4 (and_4_out, D3, D1);
  and and_5 (and_5_out, not_3_out, D3);
  or or_1 (S5, and_1_out, and_2_out, and_5_out, and_3_out, and_4_out);
endmodule

module HEX6 (
  input  D0,
  input  D1,
  input  D2,
  input  D3,
  output S6
);

  wire and_1_out, and_2_out, and_3_out, not_1_out, not_2_out, not_3_out;

  not not_1 (not_1_out, D0);
  not not_2 (not_2_out, D1);
  not not_3 (not_3_out, D2);
  and and_1 (and_1_out, not_2_out, D2);
  and and_2 (and_2_out, not_1_out, D1);
  and and_3 (and_3_out, not_3_out, D1);
  or or_1 (S6, and_1_out, and_2_out, and_3_out, D3);
endmodule

module HEX_DECODER (
  input  D0,
  input  D1,
  input  D2,
  input  D3,
  output s0,
  output s1,
  output s2,
  output s3,
  output s4,
  output s5,
  output s6
);

  HEX0 hex0_1 (.D0(D0), .D1(D1), .D2(D2), .D3(D3), .S0(s0));
  HEX1 hex1_1 (.D0(D0), .D1(D1), .D2(D2), .D3(D3), .S1(s1));
  HEX3 hex3_1 (.D0(D0), .D1(D1), .D2(D2), .D3(D3), .S3(s3));
  HEX4 hex4_1 (.D0(D0), .D1(D1), .D2(D2), .D3(D3), .S4(s4));
  HEX5 hex5_1 (.D0(D0), .D1(D1), .D2(D2), .D3(D3), .S5(s5));
  HEX6 hex6_1 (.D0(D0), .D1(D1), .D2(D2), .D3(D3), .S6(s6));
  HEX2 hex2_1 (.D0(D0), .D1(D1), .D2(D2), .D3(D3), .S2(s2));
endmodule
