// Logisim project lab3_forlab.circ as structural Verilog: 18 circuits, main circuit main
module main (
  input  [3:0] A,
  input  [2:0] op,
  input  [3:0] B
);

  wire hex_decoder_1_s0, hex_decoder_1_s1, hex_decoder_1_s2, hex_decoder_1_s3, hex_decoder_1_s4,
       hex_decoder_1_s5, hex_decoder_1_s6, hex_decoder_2_s0, hex_decoder_2_s1, hex_decoder_2_s2,
       hex_decoder_2_s3, hex_decoder_2_s4, hex_decoder_2_s5, hex_decoder_2_s6, hex_decoder_3_s0,
       hex_decoder_3_s1, hex_decoder_3_s2, hex_decoder_3_s3, hex_decoder_3_s4, hex_decoder_3_s5,
       hex_decoder_3_s6, hex_decoder_4_s0, hex_decoder_4_s1, hex_decoder_4_s2, hex_decoder_4_s3,
       hex_decoder_4_s4, hex_decoder_4_s5, hex_decoder_4_s6;
  wire [7:0] alu_1_aluout;

  HEX_DECODER hex_decoder_1 (
    .D(A), .s0(hex_decoder_1_s0), .s1(hex_decoder_1_s1), .s2(hex_decoder_1_s2), .s3(hex_decoder_1_s3),
    .s4(hex_decoder_1_s4), .s5(hex_decoder_1_s5), .s6(hex_decoder_1_s6));
  ALU alu_1 (.A(A), .B(B), .op(op), .ALUout(alu_1_aluout));
  HEX_DECODER hex_decoder_2 (
    .D(B), .s0(hex_decoder_2_s0), .s1(hex_decoder_2_s1), .s2(hex_decoder_2_s2), .s3(hex_decoder_2_s3),
    .s4(hex_decoder_2_s4), .s5(hex_decoder_2_s5), .s6(hex_decoder_2_s6));
  _7_Segment_Display HEXA (
    .g(hex_decoder_1_s6), .f(hex_decoder_1_s5), .a(hex_decoder_1_s0), .b(hex_decoder_1_s1),
    .e(hex_decoder_1_s4), .d(hex_decoder_1_s3), .c(hex_decoder_1_s2));  // open: dp
  _7_Segment_Display HEXB (
    .g(hex_decoder_2_s6), .f(hex_decoder_2_s5), .a(hex_decoder_2_s0), .b(hex_decoder_2_s1),
    .e(hex_decoder_2_s4), .d(hex_decoder_2_s3), .c(hex_decoder_2_s2));  // open: dp
  HEX_DECODER hex_decoder_3 (
    .D(alu_1_aluout[3:0]), .s0(hex_decoder_3_s0), .s1(hex_decoder_3_s1), .s2(hex_decoder_3_s2),
    .s3(hex_decoder_3_s3), .s4(hex_decoder_3_s4), .s5(hex_decoder_3_s5), .s6(hex_decoder_3_s6));
  HEX_DECODER hex_decoder_4 (
    .D(alu_1_aluout[7:4]), .s0(hex_decoder_4_s0), .s1(hex_decoder_4_s1), .s2(hex_decoder_4_s2),
    .s3(hex_decoder_4_s3), .s4(hex_decoder_4_s4), .s5(hex_decoder_4_s5), .s6(hex_decoder_4_s6));
  _7_Segment_Display HEXALU0 (
    .g(hex_decoder_3_s6), .f(hex_decoder_3_s5), .a(hex_decoder_3_s0), .b(hex_decoder_3_s1),
    .e(hex_decoder_3_s4), .d(hex_decoder_3_s3), .c(hex_decoder_3_s2));  // open: dp
  _7_Segment_Display HEXALU1 (
    .g(hex_decoder_4_s6), .f(hex_decoder_4_s5), .a(hex_decoder_4_s0), .b(hex_decoder_4_s1),
    .e(hex_decoder_4_s4), .d(hex_decoder_4_s3), .c(hex_decoder_4_s2));  // open: dp
endmodule

module full_adder (
  input  A,
  input  B,
  input  Cin,
  output Cout,
  output S
);

  wire and_1_out, and_2_out, xor_1_out;

  and and_1 (and_1_out, A, B);
  xor xor_1 (xor_1_out, A, B);
  and and_2 (and_2_out, xor_1_out, Cin);
  xor xor_2 (S, xor_1_out, Cin);
  or or_1 (Cout, and_1_out, and_2_out);
endmodule

module ripple_carry4 (
  input  [3:0] A,
  input  Cin,
  input  [3:0] B,
  output [3:0] S,
  output Cout
);

  wire full_adder_1_cout, full_adder_2_cout, full_adder_3_cout;

  full_adder full_adder_1 (.A(A[0]), .B(B[0]), .Cin(Cin), .Cout(full_adder_1_cout), .S(S[0]));
  full_adder full_adder_2 (.A(A[1]), .B(B[1]), .Cin(full_adder_1_cout), .Cout(full_adder_2_cout), .S(S[1]));
  full_adder full_adder_3 (.A(A[2]), .B(B[2]), .Cin(full_adder_2_cout), .Cout(full_adder_3_cout), .S(S[2]));
  full_adder full_adder_4 (.A(A[3]), .B(B[3]), .Cin(full_adder_3_cout), .Cout(Cout), .S(S[3]));
endmodule

module op0 (
  input  [3:0] A,
  output [7:0] OPout
);

  wire [3:0] ripple_carry4_1_s;
  wire [4:4] bit_extender_1_out;

  ripple_carry4 ripple_carry4_1 (.A(A), .B(4'b0001), .S(ripple_carry4_1_s), .Cout(OPout[4]));  // open: Cin
  assign {OPout[7:5], bit_extender_1_out[4], OPout[3:0]} = {{4{1'b0}}, ripple_carry4_1_s};  // Bit_Extender bit_extender_1
endmodule

module op1 (
  input  [3:0] A,
  input  [3:0] B,
  output [7:0] OPout
);

  wire [3:0] ripple_carry4_1_s;
  wire [4:4] bit_extender_1_out;

  ripple_carry4 ripple_carry4_1 (.A(A), .B(B), .S(ripple_carry4_1_s), .Cout(OPout[4]));  // open: Cin
  assign {OPout[7:5], bit_extender_1_out[4], OPout[3:0]} = {{4{1'b0}}, ripple_carry4_1_s};  // Bit_Extender bit_extender_1
endmodule

module op2 (
  input  [3:0] A,
  input  [3:0] B,
  output [7:0] OPout
);

  wire [3:0] adder_1_out;
  wire [4:4] bit_extender_1_out;

  Adder #(.width(4)) adder_1 (.a(A), .b(B), .out(adder_1_out), .cout(OPout[4]));  // open: cin
  assign {OPout[7:5], bit_extender_1_out[4], OPout[3:0]} = {{4{1'b0}}, adder_1_out};  // Bit_Extender bit_extender_1
endmodule

module op3 (
  input  [3:0] A,
  input  [3:0] B,
  output [7:0] OPout
);

  assign OPout[3:0] = A ^ B;  // XOR_Gate xor_1, 4 bits wide
  assign OPout[7:4] = A | B;  // OR_Gate or_1, 4 bits wide
endmodule

module op4 (
  input  [3:0] A,
  input  [3:0] B,
  output [7:0] OPout
);

  wire or_1_out;
  wire [7:0] bit_extender_1_out, bit_extender_2_out;

  assign bit_extender_1_out = {{4{1'b0}}, A};  // Bit_Extender bit_extender_1
  assign bit_extender_2_out = {{4{1'b0}}, B};  // Bit_Extender bit_extender_2
  or or_1 (or_1_out, bit_extender_2_out[7], bit_extender_2_out[6], bit_extender_2_out[5], bit_extender_2_out[4], bit_extender_2_out[3], bit_extender_2_out[2], bit_extender_2_out[1], bit_extender_2_out[0], bit_extender_1_out[7], bit_extender_1_out[6], bit_extender_1_out[5], bit_extender_1_out[4], bit_extender_1_out[3], bit_extender_1_out[2], bit_extender_1_out[1], bit_extender_1_out[0]);
  assign OPout = {{7{1'b0}}, or_1_out};  // Bit_Extender bit_extender_3
endmodule

module op5 (
  input  [3:0] B,
  input  [3:0] A,
  output [7:0] OPout
);


  assign OPout = {A, B};
endmodule

module ALU (
  input  [3:0] A,
  input  [3:0] B,
  input  [2:0] op,
  output [7:0] ALUout
);

  wire [7:0] op0_1_opout, op1_1_opout, op2_1_opout, op3_1_opout, op4_1_opout, op5_1_opout;

  op0 op0_1 (.A(A), .OPout(op0_1_opout));
  op1 op1_1 (.A(A), .B(B), .OPout(op1_1_opout));
  op2 op2_1 (.A(A), .B(B), .OPout(op2_1_opout));
  op3 op3_1 (.A(A), .B(B), .OPout(op3_1_opout));
  op4 op4_1 (.A(A), .B(B), .OPout(op4_1_opout));
  op5 op5_1 (.B(B), .A(A), .OPout(op5_1_opout));
  Multiplexer #(.select(3), .width(8), .enable("false")) multiplexer_1 (
    .in0(op0_1_opout), .in1(op1_1_opout), .in2(op2_1_opout), .in3(op3_1_opout), .in4(op4_1_opout),
    .in5(op5_1_opout), .out(ALUout), .sel(op));  // open: in6, in7
endmodule

module HEX0 (
  input  D0,
  input  D1,
  input  D2,
  input  D3,
  output S0
);

  wire and_1_out, and_2_out, and_3_out, and_4_out, and_5_out, and_6_out, not_1_out, not_2_out, not_3_out,
       not_4_out;

  not not_1 (not_1_out, D0);
  not not_2 (not_2_out, D1);
  not not_3 (not_3_out, D2);
  not not_4 (not_4_out, D3);
  and and_1 (and_1_out, not_3_out, not_2_out, D3);
  and and_2 (and_2_out, not_4_out, D0, D2);
  and and_3 (and_3_out, not_1_out, not_3_out);
  and and_4 (and_4_out, not_1_out, D1);
  and and_5 (and_5_out, not_4_out, D1);
  and and_6 (and_6_out, D1, D2);
  or or_1 (S0, and_1_out, and_2_out, and_3_out, and_4_out, and_5_out, and_6_out);
endmodule

module HEX1 (
  input  D0,
  input  D1,
  input  D2,
  input  D3,
  output S1
);

  wire and_1_out, and_2_out, and_3_out, and_4_out, and_5_out, and_6_out, not_1_out, not_2_out, not_3_out,
       not_4_out;

  not not_1 (not_1_out, D0);
  not not_2 (not_2_out, D1);
  not not_3 (not_3_out, D2);
  not not_4 (not_4_out, D3);
  and and_1 (and_1_out, D0, D1, not_4_out);
  and and_2 (and_2_out, D0, D3, not_2_out);
  and and_3 (and_3_out, not_2_out, not_1_out, not_4_out);
  and and_4 (and_4_out, not_3_out, not_1_out);
  and and_5 (and_5_out, not_2_out, not_3_out);
  and and_6 (and_6_out, not_4_out, not_3_out);
  or or_1 (S1, and_1_out, and_2_out, and_3_out, and_4_out, and_5_out, and_6_out);
endmodule

module HEX2 (
  input  D0,
  input  D1,
  input  D2,
  input  D3,
  output S2
);

  wire and_1_out, and_2_out, and_3_out, and_4_out, and_5_out, not_1_out, not_2_out, not_3_out;

  not not_1 (not_1_out, D1);
  not not_2 (not_2_out, D2);
  not not_3 (not_3_out, D3);
  and and_1 (and_1_out, not_2_out, D3);
  and and_2 (and_2_out, not_3_out, D2);
  and and_3 (and_3_out, not_2_out, D0);
  and and_4 (and_4_out, D0, not_1_out);
  and and_5 (and_5_out, not_2_out, not_1_out);
  or or_1 (S2, and_2_out, and_4_out, and_5_out, and_3_out, and_1_out);
endmodule

module HEX3 (
  input  D0,
  input  D1,
  input  D2,
  input  D3,
  output S3
);

  wire and_1_out, and_2_out, and_3_out, and_4_out, and_5_out, not_1_out, not_2_out, not_3_out, not_4_out;

  not not_1 (not_1_out, D0);
  not not_2 (not_2_out, D1);
  not not_3 (not_3_out, D2);
  not not_4 (not_4_out, D3);
  and and_1 (and_1_out, D1, D0, not_3_out);
  and and_2 (and_2_out, not_1_out, not_3_out, not_4_out);
  and and_3 (and_3_out, not_1_out, D1, D2);
  and and_4 (and_4_out, not_2_out, D0, D2);
  and and_5 (and_5_out, D3, not_2_out);
  or or_1 (S3, and_2_out, and_3_out, and_4_out, and_1_out, and_5_out);
endmodule

module HEX4 (
  input  D0,
  input  D1,
  input  D2,
  input  D3,
  output S4
);

  wire and_1_out, and_2_out, and_3_out, and_4_out, not_1_out, not_2_out;

  not not_1 (not_1_out, D0);
  not not_2 (not_2_out, D2);
  and and_1 (and_1_out, D0, D1, D3);
  and and_2 (and_2_out, D2, D3);
  and and_3 (and_3_out, D1, not_1_out);
  and and_4 (and_4_out, not_1_out, not_2_out);
  or or_1 (S4, and_1_out, and_2_out, and_3_out, and_4_out);
endmodule

module HEX5 (
  input  D0,
  input  D1,
  input  D2,
  input  D3,
  output S5
);

  wire and_1_out, and_2_out, and_3_out, and_4_out, and_5_out, not_1_out, not_2_out, not_3_out, not_4_out;

  not not_1 (not_1_out, D0);
  not not_2 (not_2_out, D1);
  not not_3 (not_3_out, D2);
  not not_4 (not_4_out, D3);
  and and_1 (and_1_out, not_1_out, D1, D2);
  and and_2 (and_2_out, not_4_out, not_2_out, D2);
  and and_3 (and_3_out, not_2_out, not_1_out, not_4_out);
  and and_4 (and_4_out, D3, D1);
  and and_5 (and_5_out, not_3_out, D3);
  or or_1 (S5, and_1_out, and_2_out, and_5_out, and_3_out, and_4_out);
endmodule

module HEX6 (
  input  D0,
  input  D1,
  input  D2,
  input  D3,
  output S6
);

  wire and_1_out, and_2_out, and_3_out, not_1_out, not_2_out, not_3_out;

  not not_1 (not_1_out, D0);
  not not_2 (not_2_out, D1);
  not not_3 (not_3_out, D2);
  and and_1 (and_1_out, not_2_out, D2);
  and and_2 (and_2_out, not_1_out, D1);
  and and_3 (and_3_out, not_3_out, D1);
  or or_1 (S6, and_1_out, and_2_out, and_3_out, D3);
endmodule

module HEX_DECODER (
  input  [3:0] D,
  output s0,
  output s1,
  output s2,
  output s3,
  output s4,
  output s5,
  output s6
);

  HEX0 hex0_1 (.D0(D[0]), .D1(D[1]), .D2(D[2]), .D3(D[3]), .S0(s0));
  HEX1 hex1_1 (.D0(D[0]), .D1(D[1]), .D2(D[2]), .D3(D[3]), .S1(s1));
  HEX3 hex3_1 (.D0(D[0]), .D1(D[1]), .D2(D[2]), .D3(D[3]), .S3(s3));
  HEX4 hex4_1 (.D0(D[0]), .D1(D[1]), .D2(D[2]), .D3(D[3]), .S4(s4));
  HEX5 hex5_1 (.D0(D[0]), .D1(D[1]), .D2(D[2]), .D3(D[3]), .S5(s5));
  HEX6 hex6_1 (.D0(D[0]), .D1(D[1]), .D2(D[2]), .D3(D[3]), .S6(s6));
  HEX2 hex2_1 (.D0(D[0]), .D1(D[1]), .D2(D[2]), .D3(D[3]), .S2(s2));
endmodule
