// Logisim project lab4_part1.circ as structural Verilog: 2 circuits, main circuit main
module main (
  input  Clk,
  input  D,
  output Q
);

  wire gated_d_latch_1_qa, n7400_1_p4;

  // _7400 7400_1: pin names not known; wires that end beside it: 1'b1, Clk, Clk, n7400_1_p4, 1'b0
  Gated_D_Latch gated_d_latch_1 (.Clk(Clk), .D(D), .Qa(gated_d_latch_1_qa));  // open: Qb
  Gated_D_Latch gated_d_latch_2 (.Clk(n7400_1_p4), .D(gated_d_latch_1_qa), .Qa(Q));  // open: Qb
endmodule

module Gated_D_Latch (
  input  Clk,
  input  D,
  output Qa,
  output Qb
);

  wire n7400_1_p4, n7400_2_pin3, n7400_2_pin6;

  // _7400 7400_1: pin names not known; wires that end beside it: 1'b1, Clk, Clk, n7400_1_p4, 1'b0
  _7400 u_7400_2 (
    .pin1(Clk), .pin2(D), .pin3(n7400_2_pin3), .pin4(n7400_1_p4), .pin5(D), .pin6(n7400_2_pin6), .pin13(Qb),
    .pin12(n7400_2_pin3), .pin11(Qa), .pin10(Qa), .pin9(n7400_2_pin6), .pin8(Qb));
endmodule
