// Logisim project lab4_part2.circ as structural Verilog: 20 circuits, main circuit main
module main (
  input  [3:0] A,
  input  [2:0] op,
  input  clk
);

  wire HEXA_s0, HEXA_s1, HEXA_s2, HEXA_s3, HEXA_s4, HEXA_s5, HEXA_s6, HEXALU0_s0, HEXALU0_s1, HEXALU0_s2,
       HEXALU0_s3, HEXALU0_s4, HEXALU0_s5, HEXALU0_s6, HEXALU1_s0, HEXALU1_s1, HEXALU1_s2, HEXALU1_s3,
       HEXALU1_s4, HEXALU1_s5, HEXALU1_s6;
  wire [3:0] bit_extender_1_out, bit_extender_1_out_2, undriven;
  wire [7:0] alu_1_aluout;

  assign {bit_extender_1_out_2, bit_extender_1_out} = {{4{undriven[3]}}, undriven};  // Bit_Extender bit_extender_1
  HEX_DECODER HEXA (
    .D(A), .s0(HEXA_s0), .s1(HEXA_s1), .s2(HEXA_s2), .s3(HEXA_s3), .s4(HEXA_s4), .s5(HEXA_s5), .s6(HEXA_s6));
  ALU alu_1 (.A(A), .B(undriven), .op(op), .ALUout(alu_1_aluout));
  Register ALUreg (.D(alu_1_aluout), .clk(clk), .Q({bit_extender_1_out_2, bit_extender_1_out}));  // open: en, clr
  _7_Segment_Display u_7_segment_display_1 (
    .g(HEXA_s6), .f(HEXA_s5), .a(HEXA_s0), .b(HEXA_s1), .e(HEXA_s4), .d(HEXA_s3), .c(HEXA_s2));  // open: dp
  HEX_DECODER HEXALU1 (
    .D(bit_extender_1_out), .s0(HEXALU1_s0), .s1(HEXALU1_s1), .s2(HEXALU1_s2), .s3(HEXALU1_s3),
    .s4(HEXALU1_s4), .s5(HEXALU1_s5), .s6(HEXALU1_s6));
  HEX_DECODER HEXALU0 (
    .D(bit_extender_1_out_2), .s0(HEXALU0_s0), .s1(HEXALU0_s1), .s2(HEXALU0_s2), .s3(HEXALU0_s3),
    .s4(HEXALU0_s4), .s5(HEXALU0_s5), .s6(HEXALU0_s6));
  _7_Segment_Display HEX_ALU1 (
    .g(HEXALU1_s6), .f(HEXALU1_s5), .a(HEXALU1_s0), .b(HEXALU1_s1), .e(HEXALU1_s4), .d(HEXALU1_s3),
    .c(HEXALU1_s2));  // open: dp
  _7_Segment_Display HEX_ALU0 (
    .g(HEXALU0_s6), .f(HEXALU0_s5), .a(HEXALU0_s0), .b(HEXALU0_s1), .e(HEXALU0_s4), .d(HEXALU0_s3),
    .c(HEXALU0_s2));  // open: dp
endmodule

module full_adder (
  input  A,
  input  B,
  input  Cin,
  output Cout,
  output S
);

  wire and_1_out, and_2_out, xor_1_out;

  and and_1 (and_1_out, A, B);
  and and_2 (and_2_out, xor_1_out, Cin);
  or or_1 (Cout, and_1_out, and_2_out);
  xor xor_1 (xor_1_out, A, B);
  xor xor_2 (S, xor_1_out, Cin);
endmodule

module ripple_carry4 (
  input  [3:0] A,
  input  [3:0] B,
  input  Cin,
  output [3:0] S,
  output Cout
);

  wire full_adder_1_cout, full_adder_2_cout, full_adder_3_cout;

  full_adder full_adder_1 (.A(A[0]), .B(B[0]), .Cin(Cin), .Cout(full_adder_1_cout), .S(S[0]));
  full_adder full_adder_2 (.A(A[1]), .B(B[1]), .Cin(full_adder_1_cout), .Cout(full_adder_2_cout), .S(S[1]));
  full_adder full_adder_3 (.A(A[2]), .B(B[2]), .Cin(full_adder_2_cout), .Cout(full_adder_3_cout), .S(S[2]));
  full_adder full_adder_4 (.A(A[3]), .B(B[3]), .Cin(full_adder_3_cout), .Cout(Cout), .S(S[3]));
endmodule

module op0 (
  input  [3:0] A,
  input  Cin,
  output [7:0] ALUout
);

  ripple_carry4 ripple_carry4_1 (.A(A), .B(4'b0001), .Cin(Cin), .S(ALUout[3:0]), .Cout(ALUout[4]));

  assign ALUout[7:5] = 3'b000;
endmodule

module op1 (
  input  [3:0] A,
  input  [3:0] B,
  input  Cin,
  output [7:0] ALUout
);

  ripple_carry4 ripple_carry4_1 (.A(A), .B(B), .Cin(Cin), .S(ALUout[3:0]), .Cout(ALUout[4]));

  assign ALUout[7:5] = 3'b000;
endmodule

module op2 (
  input  [3:0] A,
  input  [3:0] B,
  input  Cin,
  output [7:0] ALUout
);

  Adder #(.width(4)) adder_1 (.a(A), .b(B), .out(ALUout[3:0]), .cin(Cin), .cout(ALUout[4]));

  assign ALUout[7:5] = 3'b000;
endmodule

module op3 (
  input  [3:0] A,
  input  [3:0] B,
  output [7:0] ALUout
);

  xor xor_1 (ALUout[0], A[0], B[0]);
  xor xor_2 (ALUout[1], A[1], B[1]);
  xor xor_3 (ALUout[2], A[2], B[2]);
  xor xor_4 (ALUout[3], A[3], B[3]);
  or or_1 (ALUout[4], A[0], B[0]);
  or or_2 (ALUout[5], A[1], B[1]);
  or or_3 (ALUout[6], A[2], B[2]);
  or or_4 (ALUout[7], A[3], B[3]);
endmodule

module op4 (
  input  [3:0] A,
  input  [3:0] B,
  output [7:0] ALUout
);

  wire or_1_out, or_2_out, or_3_out, or_4_out, or_5_out, or_6_out, or_7_out, or_8_out, or_9_out;

  or or_1 (or_1_out, A[0], B[0]);
  or or_2 (or_2_out, A[1], B[1]);
  or or_3 (or_3_out, A[2], B[2]);
  or or_4 (or_4_out, A[3], B[3]);
  or or_5 (or_5_out, A[0], B[0]);
  or or_6 (or_6_out, A[1], B[1]);
  or or_7 (or_7_out, A[2], B[2]);
  or or_8 (or_8_out, A[3], B[3]);
  or or_9 (or_9_out, or_1_out, or_2_out, or_3_out, or_4_out, or_5_out, or_6_out, or_7_out, or_8_out);
  assign ALUout = {{7{1'b0}}, or_9_out};  // Bit_Extender bit_extender_1
endmodule

module op5 (
  input  [3:0] B,
  input  [3:0] A,
  output [7:0] OPout
);

  wire [2:0] bit_extender_2_out;
  wire [7:0] bit_extender_1_out;

  assign bit_extender_1_out = {{4{1'b0}}, B};  // Bit_Extender bit_extender_1
  Bit_Extender #(.in_width(4), .out_width(3), .\type ("zero")) bit_extender_2 (.in(A), .out(bit_extender_2_out));
  Shifter shifter_1 (.in(bit_extender_1_out), .\dist (bit_extender_2_out), .out(OPout));
endmodule

module ALU (
  input  [3:0] A,
  input  [3:0] B,
  input  [2:0] op,
  output [7:0] ALUout
);

  wire [7:0] op0_1_aluout, op1_1_aluout, op2_1_aluout, op3_1_aluout, op4_1_aluout, op5_1_opout, op6_1_opout,
       op7_1_opout;

  op0 op0_1 (.A(A), .ALUout(op0_1_aluout));  // open: Cin
  op1 op1_1 (.A(A), .B(B), .ALUout(op1_1_aluout));  // open: Cin
  op2 op2_1 (.A(A), .B(B), .ALUout(op2_1_aluout));  // open: Cin
  op3 op3_1 (.A(A), .B(B), .ALUout(op3_1_aluout));
  op4 op4_1 (.A(A), .B(B), .ALUout(op4_1_aluout));
  op5 op5_1 (.B(B), .A(A), .OPout(op5_1_opout));
  op6 op6_1 (.B(B), .A(A), .OPout(op6_1_opout));
  op7 op7_1 (.A(A), .B(B), .OPout(op7_1_opout));
  Multiplexer #(.enable("false"), .select(3), .width(8)) multiplexer_1 (
    .in0(op0_1_aluout), .in1(op1_1_aluout), .in2(op2_1_aluout), .in3(op3_1_aluout), .in4(op4_1_aluout),
    .in5(op5_1_opout), .in6(op6_1_opout), .in7(op7_1_opout), .out(ALUout), .sel(op));
endmodule

module HEX0 (
  input  D0,
  input  D1,
  input  D2,
  input  D3,
  output S0
);

  wire and_1_out, and_2_out, and_3_out, and_4_out, and_5_out, and_6_out, not_1_out, not_2_out, not_3_out,
       not_4_out;

  not not_1 (not_1_out, D0);
  not not_2 (not_2_out, D1);
  not not_3 (not_3_out, D2);
  not not_4 (not_4_out, D3);
  and and_1 (and_1_out, not_3_out, not_2_out, D3);
  and and_2 (and_2_out, not_4_out, D0, D2);
  and and_3 (and_3_out, not_1_out, not_3_out);
  and and_4 (and_4_out, not_1_out, D1);
  and and_5 (and_5_out, not_4_out, D1);
  and and_6 (and_6_out, D1, D2);
  or or_1 (S0, and_1_out, and_2_out, and_3_out, and_4_out, and_5_out, and_6_out);
endmodule

module HEX1 (
  input  D0,
  input  D1,
  input  D2,
  input  D3,
  output S1
);

  wire and_1_out, and_2_out, and_3_out, and_4_out, and_5_out, and_6_out, not_1_out, not_2_out, not_3_out,
       not_4_out;

  not not_1 (not_1_out, D0);
  not not_2 (not_2_out, D1);
  not not_3 (not_3_out, D2);
  not not_4 (not_4_out, D3);
  and and_1 (and_1_out, D0, D1, not_4_out);
  and and_2 (and_2_out, D0, D3, not_2_out);
  and and_3 (and_3_out, not_2_out, not_1_out, not_4_out);
  and and_4 (and_4_out, not_3_out, not_1_out);
  and and_5 (and_5_out, not_2_out, not_3_out);
  and and_6 (and_6_out, not_4_out, not_3_out);
  or or_1 (S1, and_1_out, and_2_out, and_3_out, and_4_out, and_5_out, and_6_out);
endmodule

module HEX2 (
  input  D0,
  input  D1,
  input  D2,
  input  D3,
  output S2
);

  wire and_1_out, and_2_out, and_3_out, and_4_out, and_5_out, not_1_out, not_2_out, not_3_out;

  not not_1 (not_1_out, D1);
  not not_2 (not_2_out, D2);
  not not_3 (not_3_out, D3);
  and and_1 (and_1_out, not_2_out, D3);
  and and_2 (and_2_out, not_3_out, D2);
  and and_3 (and_3_out, not_2_out, D0);
  and and_4 (and_4_out, D0, not_1_out);
  and and_5 (and_5_out, not_2_out, not_1_out);
  or or_1 (S2, and_2_out, and_4_out, and_5_out, and_3_out, and_1_out);
endmodule

module HEX3 (
  input  D0,
  input  D1,
  input  D2,
  input  D3,
  output S3
);

  wire and_1_out, and_2_out, and_3_out, and_4_out, and_5_out, not_1_out, not_2_out, not_3_out, not_4_out;

  not not_1 (not_1_out, D0);
  not not_2 (not_2_out, D1);
  not not_3 (not_3_out, D2);
  not not_4 (not_4_out, D3);
  and and_1 (and_1_out, D1, D0, not_3_out);
  and and_2 (and_2_out, not_1_out, not_3_out, not_4_out);
  and and_3 (and_3_out, not_1_out, D1, D2);
  and and_4 (and_4_out, not_2_out, D0, D2);
  and and_5 (and_5_out, D3, not_2_out);
  or or_1 (S3, and_2_out, and_3_out, and_4_out, and_1_out, and_5_out);
endmodule

module HEX4 (
  input  D0,
  input  D1,
  input  D2,
  input  D3,
  output S4
);

  wire and_1_out, and_2_out, and_3_out, and_4_out, not_1_out, not_2_out;

  not not_1 (not_1_out, D0);
  not not_2 (not_2_out, D2);
  and and_1 (and_1_out, D0, D1, D3);
  and and_2 (and_2_out, D2, D3);
  and and_3 (and_3_out, D1, not_1_out);
  and and_4 (and_4_out, not_1_out, not_2_out);
  or or_1 (S4, and_1_out, and_2_out, and_3_out, and_4_out);
endmodule

module HEX5 (
  input  D0,
  input  D1,
  input  D2,
  input  D3,
  output S5
);

  wire and_1_out, and_2_out, and_3_out, and_4_out, and_5_out, not_1_out, not_2_out, not_3_out, not_4_out;

  not not_1 (not_1_out, D0);
  not not_2 (not_2_out, D1);
  not not_3 (not_3_out, D2);
  not not_4 (not_4_out, D3);
  and and_1 (and_1_out, not_1_out, D1, D2);
  and and_2 (and_2_out, not_4_out, not_2_out, D2);
  and and_3 (and_3_out, not_2_out, not_1_out, not_4_out);
  and and_4 (and_4_out, D3, D1);
  and and_5 (and_5_out, not_3_out, D3);
  or or_1 (S5, and_1_out, and_2_out, and_5_out, and_3_out, and_4_out);
endmodule

module HEX6 (
  input  D0,
  input  D1,
  input  D2,
  input  D3,
  output S6
);

  wire and_1_out, and_2_out, and_3_out, not_1_out, not_2_out, not_3_out;

  not not_1 (not_1_out, D0);
  not not_2 (not_2_out, D1);
  not not_3 (not_3_out, D2);
  and and_1 (and_1_out, not_2_out, D2);
  and and_2 (and_2_out, not_1_out, D1);
  and and_3 (and_3_out, not_3_out, D1);
  or or_1 (S6, and_1_out, and_2_out, and_3_out, D3);
endmodule

module HEX_DECODER (
  input  [3:0] D,
  output s0,
  output s1,
  output s2,
  output s3,
  output s4,
  output s5,
  output s6
);

  HEX0 hex0_1 (.D0(D[0]), .D1(D[1]), .D2(D[2]), .D3(D[3]), .S0(s0));
  HEX1 hex1_1 (.D0(D[0]), .D1(D[1]), .D2(D[2]), .D3(D[3]), .S1(s1));
  HEX3 hex3_1 (.D0(D[0]), .D1(D[1]), .D2(D[2]), .D3(D[3]), .S3(s3));
  HEX4 hex4_1 (.D0(D[0]), .D1(D[1]), .D2(D[2]), .D3(D[3]), .S4(s4));
  HEX5 hex5_1 (.D0(D[0]), .D1(D[1]), .D2(D[2]), .D3(D[3]), .S5(s5));
  HEX6 hex6_1 (.D0(D[0]), .D1(D[1]), .D2(D[2]), .D3(D[3]), .S6(s6));
  HEX2 hex2_1 (.D0(D[0]), .D1(D[1]), .D2(D[2]), .D3(D[3]), .S2(s2));
endmodule

module op6 (
  input  [3:0] B,
  input  [3:0] A,
  output [7:0] OPout
);

  wire [2:0] bit_extender_2_out;
  wire [7:0] bit_extender_1_out;

  assign bit_extender_1_out = {{4{B[3]}}, B};  // Bit_Extender bit_extender_1
  Bit_Extender #(.in_width(4), .out_width(3), .\type ("zero")) bit_extender_2 (.in(A), .out(bit_extender_2_out));
  Shifter #(.shift("ar")) shifter_1 (.in(bit_extender_1_out), .\dist (bit_extender_2_out), .out(OPout));
endmodule

module op7 (
  input  [3:0] A,
  input  [3:0] B,
  output [7:0] OPout
);

  wire [7:0] bit_extender_1_out, bit_extender_2_out;

  assign bit_extender_1_out = {{4{A[3]}}, A};  // Bit_Extender bit_extender_1
  assign bit_extender_2_out = {{4{B[3]}}, B};  // Bit_Extender bit_extender_2
  Multiplier multiplier_1 (.a(bit_extender_1_out), .b(bit_extender_2_out), .out(OPout));  // open: cin, cout
endmodule
