// Logisim project lab4_part3.circ as structural Verilog
module shifter_bit (
  input  load_val,
  input  inp,
  input  shift,
  input  load_n,
  input  clk,
  input  reset,
  output Outp
);

  wire mux2to1_1_f, mux2to1_2_f;

  mux2to1 mux2to1_1 (.x(Outp), .s(shift), .y(inp), .f(mux2to1_1_f));
  mux2to1 mux2to1_2 (.x(load_val), .s(load_n), .y(mux2to1_1_f), .f(mux2to1_2_f));
  D_Flip_Flop d_ff_1 (.D(mux2to1_2_f), .clk(clk), .Q(Outp), .reset(reset));  // open: Qn, preset
endmodule

module mux2to1 (
  input  x,
  input  s,
  input  y,
  output f
);

  wire and_1_out, and_2_out, not_1_out;

  not not_1 (not_1_out, s);
  and and_1 (and_1_out, x, not_1_out);
  and and_2 (and_2_out, s, y);
  or or_1 (f, and_1_out, and_2_out);
endmodule

module shift_register (
  input  asr,
  input  [7:0] LoadVal,
  input  ShiftRight,
  input  load_n,
  input  clk,
  input  reset,
  output [7:0] out_7
);

  wire and_1_out, undriven;

  and and_1 (and_1_out, asr, LoadVal[7]);
  shifter_bit shifter_bit_1 (
    .load_val(LoadVal[0]), .inp(and_1_out), .shift(ShiftRight), .load_n(load_n), .clk(clk), .reset(reset),
    .Outp(out_7[0]));
  shifter_bit shifter_bit_2 (
    .load_val(LoadVal[1]), .inp(out_7[0]), .shift(ShiftRight), .load_n(load_n), .clk(clk), .reset(reset),
    .Outp(out_7[1]));
  shifter_bit shifter_bit_3 (
    .load_val(LoadVal[2]), .inp(out_7[1]), .shift(ShiftRight), .load_n(load_n), .clk(clk), .reset(reset),
    .Outp(out_7[2]));
  shifter_bit shifter_bit_4 (
    .load_val(LoadVal[3]), .inp(out_7[2]), .shift(ShiftRight), .load_n(load_n), .clk(clk), .reset(reset),
    .Outp(out_7[3]));
  shifter_bit shifter_bit_5 (
    .load_val(LoadVal[4]), .inp(out_7[3]), .shift(ShiftRight), .load_n(load_n), .clk(clk), .reset(reset),
    .Outp(out_7[4]));
  shifter_bit shifter_bit_6 (
    .load_val(LoadVal[5]), .inp(undriven), .shift(ShiftRight), .load_n(load_n), .clk(clk), .reset(reset),
    .Outp(out_7[5]));
  shifter_bit shifter_bit_7 (
    .load_val(LoadVal[6]), .inp(out_7[7]), .shift(ShiftRight), .load_n(load_n), .clk(clk), .reset(reset),
    .Outp(out_7[6]));
  shifter_bit shifter_bit_8 (
    .load_val(LoadVal[7]), .inp(out_7[6]), .shift(ShiftRight), .load_n(load_n), .clk(clk), .reset(reset),
    .Outp(out_7[7]));
endmodule
