// Logisim project lab5.circ as structural Verilog: 16 circuits, main circuit main
module main (
  input  Reset,
  input  Count_Enable,
  input  SW0,
  input  SW1
);

  wire Clk_out, hex_decoder_1_s0, hex_decoder_1_s1, hex_decoder_1_s2, hex_decoder_1_s3, hex_decoder_1_s4,
       hex_decoder_1_s5, hex_decoder_1_s6, ratedivider_1_out_6, undriven;
  wire [3:0] incrementer4_1_q;

  Clock Clk (.out(Clk_out));
  RateDivider ratedivider_1 (
    .Reset(Reset), .CountEnable(Count_Enable), .Clk(Clk_out), .SW0(SW0), .SW1(SW1),
    .out_6(ratedivider_1_out_6));
  incrementer4 incrementer4_1 (
    .CountEnable(ratedivider_1_out_6), .Clock(Clk_out), .Clear(undriven), .Q(incrementer4_1_q));
  HEX_DECODER hex_decoder_1 (
    .D0(incrementer4_1_q[0]), .D1(incrementer4_1_q[1]), .D2(incrementer4_1_q[2]), .D3(incrementer4_1_q[3]),
    .s0(hex_decoder_1_s0), .s1(hex_decoder_1_s1), .s2(hex_decoder_1_s2), .s3(hex_decoder_1_s3),
    .s4(hex_decoder_1_s4), .s5(hex_decoder_1_s5), .s6(hex_decoder_1_s6));
  _7_Segment_Display u_7_segment_display_1 (
    .g(hex_decoder_1_s6), .f(hex_decoder_1_s5), .a(hex_decoder_1_s0), .b(hex_decoder_1_s1),
    .e(hex_decoder_1_s4), .d(hex_decoder_1_s3), .c(hex_decoder_1_s2));  // open: dp
endmodule

module incrementer4 (
  input  CountEnable,
  input  Clock,
  input  Clear,
  output [3:0] Q
);

  wire and_1_out, and_2_out, and_3_out;

  T_Flip_Flop TFF0 (.T(CountEnable), .clk(Clock), .Q(Q[0]), .reset(Clear));  // open: Qn, preset
  and and_1 (and_1_out, CountEnable, Q[0]);
  T_Flip_Flop TFF1 (.T(and_1_out), .clk(Clock), .Q(Q[1]), .reset(Clear));  // open: Qn, preset
  and and_2 (and_2_out, and_1_out, Q[1]);
  T_Flip_Flop TFF2 (.T(and_2_out), .clk(Clock), .Q(Q[2]), .reset(Clear));  // open: Qn, preset
  and and_3 (and_3_out, and_2_out, Q[2]);
  T_Flip_Flop TFF3 (.T(and_3_out), .clk(Clock), .Q(Q[3]), .reset(Clear));  // open: Qn, preset
endmodule

module handout_example (
  input  Reset,
  input  CountEnable,
  output CounterOut
);

  wire CLK_out, not_1_out, or_1_out;
  wire [3:0] counter_1_q;

  Clock CLK (.out(CLK_out));
  not not_1 (not_1_out, CountEnable);
  or or_1 (or_1_out, CounterOut, not_1_out);
  Counter #(.max('hf), .width(4)) counter_1 (
    .clr(Reset), .load(or_1_out), .up(1'b1), .clk(CLK_out), .D(4'b0000), .Q(counter_1_q));  // open: count, carry
  and and_1 (CounterOut, counter_1_q[0], counter_1_q[1], counter_1_q[2], counter_1_q[3]);
endmodule

module counter8 (
  input  CountEnable,
  input  Clock,
  input  Clear,
  output [7:0] Q
);

  wire and_1_out, and_2_out, and_3_out, and_4_out, and_5_out, and_6_out, and_7_out, hex_decoder_1_s0,
       hex_decoder_1_s1, hex_decoder_1_s2, hex_decoder_1_s3, hex_decoder_1_s4, hex_decoder_1_s5,
       hex_decoder_1_s6, hex_decoder_2_s0, hex_decoder_2_s1, hex_decoder_2_s2, hex_decoder_2_s3,
       hex_decoder_2_s4, hex_decoder_2_s5, hex_decoder_2_s6;

  T_Flip_Flop TFF0 (.T(CountEnable), .clk(Clock), .Q(Q[0]), .reset(Clear));  // open: Qn, preset
  and and_1 (and_1_out, CountEnable, Q[0]);
  T_Flip_Flop TFF1 (.T(and_1_out), .clk(Clock), .Q(Q[1]), .reset(Clear));  // open: Qn, preset
  and and_2 (and_2_out, and_1_out, Q[1]);
  T_Flip_Flop TFF2 (.T(and_2_out), .clk(Clock), .Q(Q[2]), .reset(Clear));  // open: Qn, preset
  and and_3 (and_3_out, and_2_out, Q[2]);
  T_Flip_Flop TFF3 (.T(and_3_out), .clk(Clock), .Q(Q[3]), .reset(Clear));  // open: Qn, preset
  and and_4 (and_4_out, and_3_out, Q[3]);
  T_Flip_Flop TFF4 (.T(and_4_out), .clk(Clock), .Q(Q[4]), .reset(Clear));  // open: Qn, preset
  and and_5 (and_5_out, and_4_out, Q[4]);
  T_Flip_Flop TFF5 (.T(and_5_out), .clk(Clock), .Q(Q[5]), .reset(Clear));  // open: Qn, preset
  and and_6 (and_6_out, and_5_out, Q[5]);
  T_Flip_Flop TFF6 (.T(and_6_out), .clk(Clock), .Q(Q[6]), .reset(Clear));  // open: Qn, preset
  and and_7 (and_7_out, and_6_out, Q[6]);
  T_Flip_Flop TFF7 (.T(and_7_out), .clk(Clock), .Q(Q[7]), .reset(Clear));  // open: Qn, preset
  HEX_DECODER hex_decoder_1 (
    .D0(Q[5]), .D1(Q[5]), .D2(Q[6]), .D3(Q[7]), .s0(hex_decoder_1_s0), .s1(hex_decoder_1_s1),
    .s2(hex_decoder_1_s2), .s3(hex_decoder_1_s3), .s4(hex_decoder_1_s4), .s5(hex_decoder_1_s5),
    .s6(hex_decoder_1_s6));
  _7_Segment_Display u_7_segment_display_1 (
    .g(hex_decoder_1_s6), .f(hex_decoder_1_s5), .a(hex_decoder_1_s0), .b(hex_decoder_1_s1),
    .e(hex_decoder_1_s4), .d(hex_decoder_1_s3), .c(hex_decoder_1_s2));  // open: dp
  HEX_DECODER hex_decoder_2 (
    .D0(Q[0]), .D1(Q[1]), .D2(Q[2]), .D3(Q[3]), .s0(hex_decoder_2_s0), .s1(hex_decoder_2_s1),
    .s2(hex_decoder_2_s2), .s3(hex_decoder_2_s3), .s4(hex_decoder_2_s4), .s5(hex_decoder_2_s5),
    .s6(hex_decoder_2_s6));
  _7_Segment_Display u_7_segment_display_2 (
    .g(hex_decoder_2_s6), .f(hex_decoder_2_s5), .a(hex_decoder_2_s0), .b(hex_decoder_2_s1),
    .e(hex_decoder_2_s4), .d(hex_decoder_2_s3), .c(hex_decoder_2_s2));  // open: dp
endmodule

module HEX0 (
  input  D0,
  input  D1,
  input  D2,
  input  D3,
  output S0
);

  wire and_1_out, and_2_out, and_3_out, and_4_out, and_5_out, and_6_out, not_1_out, not_2_out, not_3_out,
       not_4_out;

  not not_1 (not_1_out, D0);
  not not_2 (not_2_out, D1);
  not not_3 (not_3_out, D2);
  not not_4 (not_4_out, D3);
  and and_1 (and_1_out, not_3_out, not_2_out, D3);
  and and_2 (and_2_out, not_4_out, D0, D2);
  and and_3 (and_3_out, not_1_out, not_3_out);
  and and_4 (and_4_out, not_1_out, D1);
  and and_5 (and_5_out, not_4_out, D1);
  and and_6 (and_6_out, D1, D2);
  or or_1 (S0, and_1_out, and_2_out, and_3_out, and_4_out, and_5_out, and_6_out);
endmodule

module HEX1 (
  input  D0,
  input  D1,
  input  D2,
  input  D3,
  output S1
);

  wire and_1_out, and_2_out, and_3_out, and_4_out, and_5_out, and_6_out, not_1_out, not_2_out, not_3_out,
       not_4_out;

  not not_1 (not_1_out, D0);
  not not_2 (not_2_out, D1);
  not not_3 (not_3_out, D2);
  not not_4 (not_4_out, D3);
  and and_1 (and_1_out, D0, D1, not_4_out);
  and and_2 (and_2_out, D0, D3, not_2_out);
  and and_3 (and_3_out, not_2_out, not_1_out, not_4_out);
  and and_4 (and_4_out, not_3_out, not_1_out);
  and and_5 (and_5_out, not_2_out, not_3_out);
  and and_6 (and_6_out, not_4_out, not_3_out);
  or or_1 (S1, and_1_out, and_2_out, and_3_out, and_4_out, and_5_out, and_6_out);
endmodule

module HEX2 (
  input  D0,
  input  D1,
  input  D2,
  input  D3,
  output S2
);

  wire and_1_out, and_2_out, and_3_out, and_4_out, and_5_out, not_1_out, not_2_out, not_3_out;

  not not_1 (not_1_out, D1);
  not not_2 (not_2_out, D2);
  not not_3 (not_3_out, D3);
  and and_1 (and_1_out, not_2_out, D3);
  and and_2 (and_2_out, not_3_out, D2);
  and and_3 (and_3_out, not_2_out, D0);
  and and_4 (and_4_out, D0, not_1_out);
  and and_5 (and_5_out, not_2_out, not_1_out);
  or or_1 (S2, and_2_out, and_4_out, and_5_out, and_3_out, and_1_out);
endmodule

module HEX3 (
  input  D0,
  input  D1,
  input  D2,
  input  D3,
  output S3
);

  wire and_1_out, and_2_out, and_3_out, and_4_out, and_5_out, not_1_out, not_2_out, not_3_out, not_4_out;

  not not_1 (not_1_out, D0);
  not not_2 (not_2_out, D1);
  not not_3 (not_3_out, D2);
  not not_4 (not_4_out, D3);
  and and_1 (and_1_out, D1, D0, not_3_out);
  and and_2 (and_2_out, not_1_out, not_3_out, not_4_out);
  and and_3 (and_3_out, not_1_out, D1, D2);
  and and_4 (and_4_out, not_2_out, D0, D2);
  and and_5 (and_5_out, D3, not_2_out);
  or or_1 (S3, and_2_out, and_3_out, and_4_out, and_1_out, and_5_out);
endmodule

module HEX4 (
  input  D0,
  input  D1,
  input  D2,
  input  D3,
  output S4
);

  wire and_1_out, and_2_out, and_3_out, and_4_out, not_1_out, not_2_out;

  not not_1 (not_1_out, D0);
  not not_2 (not_2_out, D2);
  and and_1 (and_1_out, D0, D1, D3);
  and and_2 (and_2_out, D2, D3);
  and and_3 (and_3_out, D1, not_1_out);
  and and_4 (and_4_out, not_1_out, not_2_out);
  or or_1 (S4, and_1_out, and_2_out, and_3_out, and_4_out);
endmodule

module HEX5 (
  input  D0,
  input  D1,
  input  D2,
  input  D3,
  output S5
);

  wire and_1_out, and_2_out, and_3_out, and_4_out, and_5_out, not_1_out, not_2_out, not_3_out, not_4_out;

  not not_1 (not_1_out, D0);
  not not_2 (not_2_out, D1);
  not not_3 (not_3_out, D2);
  not not_4 (not_4_out, D3);
  and and_1 (and_1_out, not_1_out, D1, D2);
  and and_2 (and_2_out, not_4_out, not_2_out, D2);
  and and_3 (and_3_out, not_2_out, not_1_out, not_4_out);
  and and_4 (and_4_out, D3, D1);
  and and_5 (and_5_out, not_3_out, D3);
  or or_1 (S5, and_1_out, and_2_out, and_5_out, and_3_out, and_4_out);
endmodule

module HEX6 (
  input  D0,
  input  D1,
  input  D2,
  input  D3,
  output S6
);

  wire and_1_out, and_2_out, and_3_out, not_1_out, not_2_out, not_3_out;

  not not_1 (not_1_out, D0);
  not not_2 (not_2_out, D1);
  not not_3 (not_3_out, D2);
  and and_1 (and_1_out, not_2_out, D2);
  and and_2 (and_2_out, not_1_out, D1);
  and and_3 (and_3_out, not_3_out, D1);
  or or_1 (S6, and_1_out, and_2_out, and_3_out, D3);
endmodule

module HEX_DECODER (
  input  D0,
  input  D1,
  input  D2,
  input  D3,
  output s0,
  output s1,
  output s2,
  output s3,
  output s4,
  output s5,
  output s6
);

  HEX0 hex0_1 (.D0(D0), .D1(D1), .D2(D2), .D3(D3), .S0(s0));
  HEX1 hex1_1 (.D0(D0), .D1(D1), .D2(D2), .D3(D3), .S1(s1));
  HEX3 hex3_1 (.D0(D0), .D1(D1), .D2(D2), .D3(D3), .S3(s3));
  HEX4 hex4_1 (.D0(D0), .D1(D1), .D2(D2), .D3(D3), .S4(s4));
  HEX5 hex5_1 (.D0(D0), .D1(D1), .D2(D2), .D3(D3), .S5(s5));
  HEX6 hex6_1 (.D0(D0), .D1(D1), .D2(D2), .D3(D3), .S6(s6));
  HEX2 hex2_1 (.D0(D0), .D1(D1), .D2(D2), .D3(D3), .S2(s2));
endmodule

module RateDivider (
  input  Reset,
  input  CountEnable,
  input  Clk,
  input  SW0,
  input  SW1,
  output out_6
);

  wire not_1_out, or_1_out;
  wire [7:0] bit_extender_1_out, counter_1_q, multiplexer_1_out;

  assign bit_extender_1_out = {{7{Clk}}, Clk};  // Bit_Extender bit_extender_1
  Multiplexer #(.enable("false"), .select(2), .width(8)) multiplexer_1 (
    .in0(bit_extender_1_out), .in1(8'h20), .in2(8'h40), .in3(8'h80), .out(multiplexer_1_out), .sel({SW1, SW0}));
  or or_1 (or_1_out, out_6, not_1_out);
  not not_1 (not_1_out, CountEnable);
  Counter counter_1 (
    .clr(Reset), .load(or_1_out), .up(1'b0), .clk(Clk), .D(multiplexer_1_out), .Q(counter_1_q));  // open: count, carry
  and and_1 (out_6, counter_1_q[0], counter_1_q[1], counter_1_q[2], counter_1_q[3], counter_1_q[4], counter_1_q[5], counter_1_q[6], counter_1_q[7]);
endmodule

module DisplayCounter (
  input  Reset,
  input  Count_Enable,
  input  SW0,
  input  SW1,
  output Q
);

  wire Clk_out, hex_decoder_1_s0, hex_decoder_1_s1, hex_decoder_1_s2, hex_decoder_1_s3, hex_decoder_1_s4,
       hex_decoder_1_s5, hex_decoder_1_s6, undriven;
  wire [3:0] incrementer4_1_q;

  Clock Clk (.out(Clk_out));
  RateDivider ratedivider_1 (.Reset(Reset), .CountEnable(Count_Enable), .Clk(Clk_out), .SW0(SW0), .SW1(SW1), .out_6(Q));
  incrementer4 incrementer4_1 (.CountEnable(Q), .Clock(Clk_out), .Clear(undriven), .Q(incrementer4_1_q));
  HEX_DECODER hex_decoder_1 (
    .D0(incrementer4_1_q[0]), .D1(incrementer4_1_q[1]), .D2(incrementer4_1_q[2]), .D3(incrementer4_1_q[3]),
    .s0(hex_decoder_1_s0), .s1(hex_decoder_1_s1), .s2(hex_decoder_1_s2), .s3(hex_decoder_1_s3),
    .s4(hex_decoder_1_s4), .s5(hex_decoder_1_s5), .s6(hex_decoder_1_s6));
  _7_Segment_Display u_7_segment_display_1 (
    .g(hex_decoder_1_s6), .f(hex_decoder_1_s5), .a(hex_decoder_1_s0), .b(hex_decoder_1_s1),
    .e(hex_decoder_1_s4), .d(hex_decoder_1_s3), .c(hex_decoder_1_s2));  // open: dp
endmodule

module MORSE_LUT (
  input  [2:0] Char,
  output [13:0] MorseCode
);

  Multiplexer #(.enable("false"), .select(3), .width(14)) multiplexer_1 (
    .in0(14'h2800), .in1(14'h2000), .in2(14'h2e00), .in3(14'h2b80), .in4(14'h3b80), .in5(14'h2ae0),
    .in6(14'h2bb8), .in7(14'h2ea0), .out(MorseCode), .sel(Char));
endmodule

module morse_code (
  input  Rst,
  input  Enable,
  input  Reset,
  input  Shift,
  input  LoadEnable,
  input  [2:0] CharSelect
);

  wire bit_extender_1_out, clock_1_out, ratedivider_1_out_6;
  wire [13:0] morse_lut_1_morsecode, shift_register_1_p18;

  Clock clock_1 (.out(clock_1_out));
  MORSE_LUT morse_lut_1 (.Char(CharSelect), .MorseCode(morse_lut_1_morsecode));
  RateDivider ratedivider_1 (
    .Reset(Rst), .CountEnable(Enable), .Clk(clock_1_out), .SW0(1'b0), .SW1(1'b1), .out_6(ratedivider_1_out_6));
  // Shift_Register #(.length(14)) shift_register_1: pin names not known; wires that end beside it: Reset, LoadEnable, Shift, ratedivider_1_out_6, 1'b0, morse_lut_1_morsecode[0], morse_lut_1_morsecode[1], morse_lut_1_morsecode[2], morse_lut_1_morsecode[3], morse_lut_1_morsecode[4], morse_lut_1_morsecode[5], morse_lut_1_morsecode[6], morse_lut_1_morsecode[7], morse_lut_1_morsecode[8], morse_lut_1_morsecode[9], morse_lut_1_morsecode[10], morse_lut_1_morsecode[11], shift_register_1_p18[0], shift_register_1_p18[1], shift_register_1_p18[2], shift_register_1_p18[3], shift_register_1_p18[4], shift_register_1_p18[5], shift_register_1_p18[6], shift_register_1_p18[7], shift_register_1_p18[8], shift_register_1_p18[9], shift_register_1_p18[10], shift_register_1_p18[11]
  Bit_Extender #(.in_width(14), .out_width(1)) bit_extender_1 (.in(shift_register_1_p18), .out(bit_extender_1_out));
  LED led_1 (.in(bit_extender_1_out));
endmodule
